// Logisim project smith-parts.circ as structural Verilog: 6 circuits, main circuit main
module main (
);

  wire and_1_out, and_2_out, and_3_out, and_4_out, clock_1_out, comparator_1_eq, comparator_2_eq,
       comparator_3_gt, divider_1_remeq, not_1_out, not_2_out, not_3_out, not_4_out;
  wire [9:0] adder_1_out, counter_1_q, digitadder_1_output, digitadder_2_output, divider_1_muxo,
       divider_1_ramo, oddgen_1_out_3, register_1_q;

  Clock clock_1 (.out(clock_1_out));
  oddgen oddgen_1 (.clk(clock_1_out), .out_3(oddgen_1_out_3), .reset(and_1_out));
  digitadder digitadder_1 (.\input (10'h29a), .\output (digitadder_1_output));  // open: clone
  and and_1 (and_1_out, not_1_out, divider_1_ramo[0], not_2_out);
  divider divider_1 (
    .\input (oddgen_1_out_3), .clock(clock_1_out), .selectline(divider_1_ramo[0]), .remeq(divider_1_remeq),
    .ramo(divider_1_ramo), .muxo(divider_1_muxo));
  not not_1 (not_1_out, divider_1_remeq);
  not not_2 (not_2_out, comparator_2_eq);
  Comparator #(.width(10)) comparator_1 (
    .a(digitadder_1_output), .b(register_1_q), .eq(comparator_1_eq));  // open: gt, lt
  and and_2 (and_2_out, divider_1_remeq, not_3_out);
  not not_3 (not_3_out, comparator_2_eq);
  Register #(.width(10)) register_1 (
    .D(adder_1_out), .en(and_2_out), .Q(register_1_q), .clk(clock_1_out));  // open: clr
  and and_3 (and_3_out, comparator_1_eq, comparator_2_eq, comparator_3_gt);
  Comparator #(.width(10)) comparator_2 (.a(divider_1_ramo), .b(10'h1), .eq(comparator_2_eq));  // open: gt, lt
  Counter #(.width(10), .max('h3ff)) counter_1 (
    .load(1'b0), .D({10{1'b0}}), .count(divider_1_remeq), .Q(counter_1_q), .clk(clock_1_out));  // open: carry, clr
  digitadder digitadder_2 (.\input (divider_1_muxo), .\output (digitadder_2_output));  // open: clone
  Adder #(.width(10)) adder_1 (.a(register_1_q), .b(digitadder_2_output), .out(adder_1_out));  // open: cin, cout
  not not_4 (not_4_out, and_3_out);
  Comparator #(.width(10)) comparator_3 (.a(counter_1_q), .b(10'h1), .gt(comparator_3_gt));  // open: eq, lt
  and and_4 (and_4_out, not_4_out, comparator_2_eq);
  LED led_1 (.in(and_3_out));
  LED led_2 (.in(and_4_out));
endmodule

module oddgen (
  input  clk,
  input  reset,
  output [9:0] out_3
);

  wire and_1_out, and_2_out, and_3_out, and_4_out, and_5_out, and_6_out, and_7_out;
  wire [9:1] t_ff_1_q;

  T_Flip_Flop t_ff_1 (.clk(clk), .T(1'b1), .Q(t_ff_1_q[1]), .en(reset));  // open: Qn, preset, reset
  T_Flip_Flop t_ff_2 (.clk(clk), .T(t_ff_1_q[1]), .Q(t_ff_1_q[2]), .en(reset));  // open: Qn, preset, reset
  and and_1 (and_1_out, t_ff_1_q[1], t_ff_1_q[2]);
  T_Flip_Flop t_ff_3 (.clk(clk), .T(and_1_out), .Q(t_ff_1_q[3]), .en(reset));  // open: Qn, preset, reset
  T_Flip_Flop t_ff_4 (.clk(clk), .T(and_2_out), .Q(t_ff_1_q[4]), .en(reset));  // open: Qn, preset, reset
  and and_2 (and_2_out, and_1_out, t_ff_1_q[3]);
  T_Flip_Flop t_ff_5 (.clk(clk), .T(and_3_out), .Q(t_ff_1_q[5]), .en(reset));  // open: Qn, preset, reset
  and and_3 (and_3_out, and_2_out, t_ff_1_q[4]);
  T_Flip_Flop t_ff_6 (.clk(clk), .T(and_4_out), .Q(t_ff_1_q[6]), .en(reset));  // open: Qn, preset, reset
  and and_4 (and_4_out, and_3_out, t_ff_1_q[5]);
  T_Flip_Flop t_ff_7 (.clk(clk), .T(and_5_out), .Q(t_ff_1_q[8]), .en(reset));  // open: Qn, preset, reset
  and and_5 (and_5_out, and_4_out, t_ff_1_q[6]);
  T_Flip_Flop t_ff_8 (.clk(clk), .T(and_6_out), .Q(t_ff_1_q[8]), .en(reset));  // open: Qn, preset, reset
  and and_6 (and_6_out, and_5_out, t_ff_1_q[8]);
  T_Flip_Flop t_ff_9 (.T(and_7_out), .Q(t_ff_1_q[9]), .en(reset));  // open: clk, Qn, preset, reset
  and and_7 (and_7_out, and_6_out, t_ff_1_q[8]);
  Adder #(.width(10)) adder_1 (
    .a(10'h2), .b({t_ff_1_q[9:8], t_ff_1_q[8], t_ff_1_q[6:1], 1'b1}), .out(out_3));  // open: cin, cout
endmodule

module digitsplitter (
  input  [9:0] in_1,
  output [9:0] msd,
  output [9:0] mr,
  output [9:0] mid,
  output [9:0] midc,
  output [9:0] lsd,
  output [9:0] lr
);

  Divider #(.width(10)) divider_1 (.a(in_1), .b(10'h3e8), .out(msd), .rem(mr));  // open: upper
  Divider #(.width(10)) divider_2 (.a(mr), .b(10'h64), .out(mid), .rem(midc));  // open: upper
  Divider #(.width(10)) divider_3 (.a(midc), .b(10'ha), .out(lsd), .rem(lr));  // open: upper
endmodule

module digitadder (
  input  [9:0] \input ,
  output [9:0] clone,
  output [9:0] \output 
);

  wire [9:0] adder_1_out, adder_2_out, digitsplitter_1_lr, digitsplitter_1_lsd, digitsplitter_1_mid,
       digitsplitter_1_msd;

  digitsplitter digitsplitter_1 (
    .in_1(\input ), .msd(digitsplitter_1_msd), .mid(digitsplitter_1_mid), .lsd(digitsplitter_1_lsd),
    .lr(digitsplitter_1_lr));  // open: mr, midc
  Adder #(.width(10)) adder_1 (.a(digitsplitter_1_msd), .b(digitsplitter_1_mid), .out(adder_1_out));  // open: cin, cout
  Adder #(.width(10)) adder_2 (.a(digitsplitter_1_lsd), .b(digitsplitter_1_lr), .out(adder_2_out));  // open: cin, cout
  Adder #(.width(10)) adder_3 (.a(adder_1_out), .b(adder_2_out), .out(\output ));  // open: cin, cout

  assign clone = \input ;
endmodule

module divider (
  input  [9:0] \input ,
  input  clock,
  input  selectline,
  output [9:0] ramo,
  output [9:0] muxo,
  output remeq
);

  wire [9:0] divider_1_out, divider_1_rem, multiplexer_2_out;

  Multiplexer #(.width(10)) multiplexer_1 (.in0(10'h2), .in1(\input ), .out(muxo), .sel(selectline));  // open: en
  Multiplexer #(.width(10)) multiplexer_2 (
    .in0(ramo), .in1(divider_1_out), .out(multiplexer_2_out), .sel(remeq));  // open: en
  RAM #(.addrWidth(2), .dataWidth(10), .bus("separate")) ram_1 (
    .addr(2'b00), .din(multiplexer_2_out), .data(ramo), .str(1'b1), .clk(clock), .ld(1'b1));  // open: sel, clr
  Divider #(.width(10)) divider_1 (.a(ramo), .b(muxo), .out(divider_1_out), .rem(divider_1_rem));  // open: upper
  Comparator #(.width(10)) comparator_1 (.a(divider_1_rem), .b({10{1'b0}}), .eq(remeq));  // open: gt, lt

  // Notes on the sheet:
  //   TO FIND PRIME FACTORS 
endmodule

module rom (
  input  in_1,
  input  in_2,
  input  in_3,
  input  in_4,
  input  in_5,
  input  in_6,
  input  in_7,
  input  in_8,
  input  in_9,
  input  in_10,
  input  in_11,
  output [9:0] out_12
);

  D_Flip_Flop d_ff_1 (.clk(in_1), .D(in_2), .Q(out_12[0]));  // open: Qn, preset, en, reset
  D_Flip_Flop d_ff_2 (.clk(in_1), .D(in_3), .Q(out_12[1]));  // open: Qn, preset, en, reset
  D_Flip_Flop d_ff_3 (.clk(in_1), .D(in_4), .Q(out_12[2]));  // open: Qn, preset, en, reset
  D_Flip_Flop d_ff_4 (.clk(in_1), .D(in_5), .Q(out_12[3]));  // open: Qn, preset, en, reset
  D_Flip_Flop d_ff_5 (.clk(in_1), .D(in_6), .Q(out_12[4]));  // open: Qn, preset, en, reset
  D_Flip_Flop d_ff_6 (.clk(in_1), .D(in_7), .Q(out_12[5]));  // open: Qn, preset, en, reset
  D_Flip_Flop d_ff_7 (.clk(in_1), .D(in_8), .Q(out_12[6]));  // open: Qn, preset, en, reset
  D_Flip_Flop d_ff_8 (.clk(in_1), .D(in_9), .Q(out_12[7]));  // open: Qn, preset, en, reset
  D_Flip_Flop d_ff_9 (.clk(in_1), .D(in_10), .Q(out_12[8]));  // open: Qn, preset, en, reset
  D_Flip_Flop d_ff_10 (.clk(in_1), .D(in_11), .Q(out_12[9]));  // open: Qn, preset, en, reset
endmodule
